# Fritzing sketch GoodLightForWorking_breadboard (saved by Fritzing 0.9.3b)
breadboards: 1

parts:
  Part1 = Arduino Uno (Rev3)
  R1 = Resistor [tolerance=±5% resistance=220 package=THT]
  R2 = Photocell (LDR) [package=THT]
  R3 = Resistor [tolerance=±5% resistance=220 package=THT]
  LED1 = LED - 5mm [color="Yellow (592nm)" package="5 mm [THT]"]
  LCD1 = LCD screen
  R5 = Resistor [tolerance=±5% resistance=220 package=THT]

nets (from the breadboard view):
  N1: Part1.D9_PWM, R3.Pin_0, R3.Pin_1, LED1.anode
  N2: Part1.D11_PWM/MOSI, LCD1.E
  N3: Part1.D12/MISO, LCD1.RS
  N4: Part1.D2, LCD1.DB7
  N5: Part1.D3_PWM, LCD1.DB6
  N6: Part1.D4, LCD1.DB5
  N7: Part1.D5_PWM, LCD1.DB4
  5V: Part1.5V, R2.pin_0, LCD1.VDD, R5.Pin_1
  GND: Part1.GND, R1.Pin_1, LED1.cathode, LCD1.VSS, LCD1.R/W, LCD1.LED-
  N8: R1.Pin_0, R2.pin_1
  N9: LCD1.LED+, R5.Pin_0
