# Fritzing sketch GoodLightForWorking_schematic (saved by Fritzing 0.9.3b)
breadboards: 1

parts:
  part = Arduino Uno (Rev3)
  R1 = Resistor [tolerance=±5% resistance=220 package=THT]
  LDR = Photocell (LDR) [package=THT]
  R2 = Resistor [tolerance=±5% resistance=220 package=THT]
  LED = LED - 5mm [color="Yellow (592nm)" package="5 mm [THT]"]
  LCD = LCD screen
  R3 = Resistor [tolerance=±5% resistance=220 package=THT]

nets:
  N1: part.D9_PWM, R2.Pin_0, R2.Pin_1, LED.anode, LCD.LED-
  N2: part.D11_PWM/MOSI, LCD.E
  N3: part.D12/MISO, LCD.RS
  N4: part.D2, LCD.DB7
  N5: part.D3_PWM, LCD.DB6
  N6: part.D4, LCD.DB5
  N7: part.D5_PWM, LCD.DB4
  N8: part.5V, LDR.pin_0, R3.Pin_1
  N9: part.GND, R1.Pin_1, LCD.R/W
  N10: R1.Pin_0, LDR.pin_1
  N11: LCD.LED+, R3.Pin_0
