# Fritzing sketch GoodLightForWorking_breadboard (saved by Fritzing 0.9.3b)
breadboards: 1

parts:
  R1 = Resistor [tolerance=±5% resistance=220 package=THT]
  R2 = Photocell (LDR) [package=THT]
  Part2 = Arduino Leonardo (Rev3b)

nets:
  N1: R1.Pin_0, R2.pin_1
  N2: R2.pin_0, Part2.5V
